// Logisim project alu.circ as structural Verilog: 5 circuits, main circuit alu
module alu (
  input  [31:0] A,
  input  [31:0] B,
  input  [3:0] ALUSel,
  output [31:0] Result
);

  wire comparator_1_lt;
  wire [31:0] add0, and12, div7, divu8, mul1, mulh4, mulhu5, or10, remu11, sll3, slt14, sra15, srl9, sub2,
       xor6;

  Multiplexer #(.select(4), .width(32), .enable("false")) multiplexer_1 (
    .in0(add0), .in1(mul1), .in2(sub2), .in3(sll3), .in4(mulh4), .in5(mulhu5), .in6(xor6), .in7(div7),
    .in8(divu8), .in9(srl9), .in10(or10), .in11(remu11), .in12(and12), .in13(B), .in14(slt14), .in15(sra15),
    .out(Result), .sel(ALUSel));
  Adder #(.width(32)) adder_1 (.a(A), .b(B), .out(add0));  // open: cin, cout
  Multiplier #(.width(32)) multiplier_1 (.a(A), .b(B), .out(mul1));  // open: cin, cout
  Subtractor #(.width(32)) subtractor_1 (.a(A), .b(B), .out(sub2));  // open: bin, bout
  Shifter #(.width(32)) shifter_1 (.in(A), .\dist (B[4:0]), .out(sll3));
  mulh mulh_1 (.in_1(A), .in_2(B), .out_3(mulh4));
  Multiplier #(.width(32)) multiplier_2 (.a(A), .b(B), .cout(mulhu5));  // open: out, cin
  assign xor6 = A ^ B;  // XOR_Gate xor_1, 32 bits wide
  div div_1 (.in_1(A), .in_2(B), .out_3(div7));
  Divider #(.width(32)) divider_1 (.a(A), .b(B), .out(divu8));  // open: upper, rem
  Shifter #(.width(32), .shift("lr")) shifter_2 (.in(A), .\dist (B[4:0]), .out(srl9));
  assign or10 = A | B;  // OR_Gate or_1, 32 bits wide
  Divider #(.width(32)) divider_2 (.a(A), .b(B), .rem(remu11));  // open: out, upper
  assign and12 = A & B;  // AND_Gate and_1, 32 bits wide
  Comparator #(.width(32)) comparator_1 (.a(A), .b(B), .lt(comparator_1_lt));  // open: gt, eq
  assign slt14 = {{31{1'b0}}, comparator_1_lt};  // Bit_Extender bit_extender_1
  Shifter #(.width(32), .shift("ar")) shifter_3 (.in(A), .\dist (B[4:0]), .out(sra15));

  // Other names for the same wires on the sheet: lui13[31:0] = B

  // Notes on the sheet:
  //   INPUTS to your circuit
  //   DON'T CHANGE THE LOCATIONS OF THE INPUTS AND OUTPUTS!
  //   OUTPUT from your circuit
endmodule

module mulh (
  input  [31:0] in_1,
  input  [31:0] in_2,
  output [31:0] out_3
);

  wire [31:0] multiplier_1_cout, multiplier_1_out, multiplier_2_out, multiplier_3_out, multiplier_4_cout,
       negator_1_out, negator_2_out;

  Multiplier #(.width(32)) multiplier_1 (
    .a(in_1), .b(in_2), .out(multiplier_1_out), .cout(multiplier_1_cout));  // open: cin
  Multiplier #(.width(32)) multiplier_2 (
    .a(in_2), .b({32{1'b1}}), .out(multiplier_2_out), .cin(multiplier_1_cout));  // open: cout
  Multiplier #(.width(32)) multiplier_3 (
    .a(in_1), .b({32{1'b1}}), .out(multiplier_3_out), .cin(multiplier_1_cout));  // open: cout
  Negator #(.width(32)) negator_1 (.in(in_1), .out(negator_1_out));
  Multiplier #(.width(32)) multiplier_4 (
    .a(negator_1_out), .b(negator_2_out), .cout(multiplier_4_cout));  // open: out, cin
  Negator #(.width(32)) negator_2 (.in(in_2), .out(negator_2_out));
  Multiplexer #(.select(2), .width(32), .enable("false")) multiplexer_1 (
    .in0(multiplier_1_cout), .in1(multiplier_2_out), .in2(multiplier_3_out), .in3(multiplier_4_cout),
    .out(out_3), .sel({in_2[31], in_1[31]}));

  // Other names for the same wires on the sheet: input1[31:0] = in_1; sign1 = in_1[31]; input2[31:0] = in_2;
  //   sign2 = in_2[31]
endmodule

module div (
  input  [31:0] in_1,
  input  [31:0] in_2,
  output [31:0] out_3
);

  wire [31:0] divider_1_out, divider_2_out, divider_3_out, divider_4_out, negator_1_out, negator_2_out,
       negator_3_out, negator_4_out;

  Negator #(.width(32)) negator_1 (.in(in_1), .out(negator_1_out));
  Negator #(.width(32)) negator_2 (.in(in_2), .out(negator_2_out));
  Divider #(.width(32)) divider_1 (.a(in_1), .b(in_2), .out(divider_1_out));  // open: upper, rem
  Divider #(.width(32)) divider_2 (.a(negator_1_out), .b(in_2), .out(divider_2_out));  // open: upper, rem
  Divider #(.width(32)) divider_3 (.a(in_1), .b(negator_2_out), .out(divider_3_out));  // open: upper, rem
  Divider #(.width(32)) divider_4 (.a(negator_1_out), .b(negator_2_out), .out(divider_4_out));  // open: upper, rem
  Negator #(.width(32)) negator_3 (.in(divider_2_out), .out(negator_3_out));
  Negator #(.width(32)) negator_4 (.in(divider_3_out), .out(negator_4_out));
  Multiplexer #(.select(2), .width(32), .enable("false")) multiplexer_1 (
    .in0(divider_1_out), .in1(negator_3_out), .in2(negator_4_out), .in3(divider_4_out), .out(out_3),
    .sel({in_2[31], in_1[31]}));

  // Other names for the same wires on the sheet: input1[31:0] = in_1; sign1 = in_1[31]; input2[31:0] = in_2;
  //   sign2 = in_2[31]
endmodule

module sir (
  input  [31:0] in_1,
  input  [31:0] in_2,
  output [31:0] out_3
);

  Comparator #(.width(32)) comparator_1 (
    .a({in_1[0], in_1[1], in_1[2], in_1[3], in_1[4], in_1[5], in_1[6], in_1[7], in_1[8], in_1[9], in_1[10], in_1[11], in_1[12], in_1[13], in_1[14], in_1[15], in_1[16], in_1[17], in_1[18], in_1[19], in_1[20], in_1[21], in_1[22], in_1[23], in_1[24], in_1[25], in_1[26], in_1[27], in_1[28], in_1[29], in_1[30], in_1[31]}),
    .b(in_2), .eq(out_3[0]));  // open: gt, lt

  assign out_3[31:1] = {31{1'b0}};
endmodule

module cnto (
  input  [31:0] in_1,
  input  [31:0] in_2,
  output [31:0] out_3
);

  wire clock_1_out, comparator_1_eq, not_1_out, not_2_out;
  wire [4:0] register_3_q;
  wire [5:0] adder_2_out, adder_3_out, adder_4_out, bitadder_1_out, bitadder_2_out, register_1_q,
       register_2_q;
  wire [5:5] register_3_q_2;
  wire [6:0] adder_1_out, bit_extender_1_out, bit_extender_2_out;
  wire [31:0] shifter_1_out;

  Shifter #(.width(32), .shift("lr")) shifter_1 (.in(in_1), .\dist (register_3_q), .out(shifter_1_out));
  BitAdder #(.width(32)) bitadder_1 (.in0(in_1), .out(bitadder_1_out));
  assign bit_extender_1_out = {{1{1'b0}}, bitadder_1_out};  // Bit_Extender bit_extender_1
  assign bit_extender_2_out = {{1{1'b0}}, bitadder_2_out};  // Bit_Extender bit_extender_2
  BitAdder #(.width(32)) bitadder_2 (.in0(in_2), .out(bitadder_2_out));
  Adder #(.width(7)) adder_1 (.a(bit_extender_1_out), .b(bit_extender_2_out), .out(adder_1_out));  // open: cin, cout
  Register #(.width(6)) register_1 (
    .D({{5{1'b0}}, in_1[0]}), .en(not_1_out), .clk(clock_1_out), .Q(register_1_q));  // open: clr
  not not_1 (not_1_out, not_2_out);
  Register #(.width(6)) register_2 (.D(adder_2_out), .en(not_2_out), .clk(clock_1_out), .Q(register_2_q));  // open: clr
  Adder #(.width(6)) adder_2 (
    .a({{5{1'b0}}, shifter_1_out[0]}), .b(register_2_q), .out(adder_2_out));  // open: cin, cout
  Clock clock_1 (.out(clock_1_out));
  Register #(.width(6)) register_3 (
    .D(adder_3_out), .en(not_2_out), .clk(clock_1_out), .Q({register_3_q_2[5], register_3_q}));  // open: clr
  Adder #(.width(6)) adder_3 (
    .a(6'b000001), .b({register_3_q_2[5], register_3_q}), .out(adder_3_out));  // open: cin, cout
  assign out_3 = {{25{1'b0}}, adder_1_out};  // Bit_Extender bit_extender_3
  Adder #(.width(6)) adder_4 (.a(register_1_q), .b(register_2_q), .out(adder_4_out));  // open: cin, cout
  Comparator #(.width(6)) comparator_1 (
    .a({register_3_q_2[5], register_3_q}), .b(6'b011111), .eq(comparator_1_eq));  // open: gt, lt
  not not_2 (not_2_out, comparator_1_eq);
endmodule
