// Logisim project cpu.circ as structural Verilog: 1 circuit, main circuit main
module main (
  input  [31:0] INSTRUCTION,
  input  CLOCK,
  output [31:0] FETCH_ADDRESS,
  output [31:0] ra,
  output [31:0] sp,
  output [31:0] t0,
  output [31:0] t1,
  output [31:0] t2,
  output [31:0] s0,
  output [31:0] s1,
  output [31:0] a0
);

  wire and_3_out, and_4_out, and_5_out, and_6_out, and_7_out, and_11_out, auipc, beq_sign, bgeu_sign,
       blt_sign, bltu_sign, bne_sign, bSel, bSelz, comparator_1_eq, comparator_2_eq, comparator_3_eq,
       comparator_4_eq, comparator_5_eq, comparator_6_eq, comparator_7_eq, comparator_8_eq, comparator_9_eq,
       comparator_10_eq, comparator_11_eq, comparator_12_eq, comparator_15_eq, comparator_16_eq,
       comparator_17_eq, comparator_18_eq, comparator_19_eq, comparator_20_eq, comparator_21_eq,
       comparator_22_eq, comparator_23_eq, comparator_24_eq, comparator_25_eq, comparator_26_eq,
       comparator_27_eq, comparator_28_eq, comparator_29_eq, comparator_30_eq, comparator_31_eq,
       comparator_32_eq, comparator_33_eq, comparator_34_eq, comparator_35_eq, comparator_36_eq,
       comparator_37_eq, comparator_38_eq, comparator_39_eq, comparator_40_eq, comparator_41_eq,
       comparator_42_eq, comparator_43_eq, comparator_44_eq, comparator_45_eq, comparator_47_eq,
       comparator_48_eq, comparator_49_eq, comparator_50_eq, comparator_51_eq, comparator_52_eq,
       comparator_53_eq, comparator_54_eq, jSel, jSelz, not_3_out, or_1_out, or_5_out, RegWEn, RegWEnz;
  wire [1:0] and_8_out, and_9_out, and_10_out, bit_extender_1_out, bit_extender_2_out, bit_extender_3_out,
       StoreSel;
  wire [2:0] func3;
  wire [3:0] ALUSel, and_13_out, and_14_out, and_15_out, and_16_out, and_17_out, and_18_out, and_19_out,
       and_20_out, and_21_out, and_22_out, and_23_out, and_24_out, and_25_out, and_26_out, and_27_out,
       and_28_out, and_29_out, and_30_out, and_31_out, and_32_out, and_33_out, and_34_out, and_35_out,
       and_36_out, and_37_out, bit_extender_6_out, bit_extender_7_out, bit_extender_8_out,
       bit_extender_9_out, bit_extender_10_out, bit_extender_11_out, bit_extender_12_out,
       bit_extender_13_out, bit_extender_14_out, bit_extender_15_out, bit_extender_16_out,
       bit_extender_17_out, bit_extender_18_out, bit_extender_19_out, bit_extender_20_out,
       bit_extender_21_out, bit_extender_22_out, bit_extender_23_out, bit_extender_24_out,
       bit_extender_25_out, bit_extender_26_out, bit_extender_27_out, bit_extender_28_out,
       bit_extender_29_out, bit_extender_30_out, Seli, Selr;
  wire [4:0] rdz;
  wire [6:0] func7;
  wire [11:0] multiplexer_6_out;
  wire [19:0] multiplexer_5_out;
  wire [20:0] multiplexer_3_out, multiplexer_4_out;
  wire [24:0] INSTRUCTIONz;
  wire [31:0] adder_1_out, adder_2_out, adder_4_out, aluz, and_1_out, and_2_out, bit_extender_4_out,
       bit_extender_5_out, imm, immz, J, jalr, Jz, load, multiplexer_1_out, multiplexer_7_out,
       multiplexer_10_out, multiplexer_11_out, multiplexer_12_out, multiplexer_13_out, multiplexer_14_out,
       multiplexer_15_out, multiplexer_16_out, multiplexer_17_out, multiplexer_18_out, PC, pcz, ReadData,
       RS1, RS2, shifter_1_out, shifter_2_out, shifter_4_out, shifter_5_out, shifter_6_out, shifter_7_out,
       shifter_8_out, shifter_9_out, shifter_10_out, shifter_11_out, uj, WriteData;

  Register #(.width(32)) register_1 (.D(PC), .clk(CLOCK), .Q(FETCH_ADDRESS));  // open: en, clr
  Register #(.width(32)) register_2 (.D(FETCH_ADDRESS), .clk(CLOCK), .Q(pcz));  // open: en, clr
  Register #(.width(1)) register_3 (.D(RegWEn), .clk(CLOCK), .Q(RegWEnz));  // open: en, clr
  Multiplexer #(.width(32), .enable("false")) multiplexer_1 (
    .in0(FETCH_ADDRESS), .in1(pcz), .out(multiplexer_1_out), .sel(bSelz));
  Adder #(.width(32)) adder_1 (.a(multiplexer_1_out), .b(32'h1), .out(adder_1_out));  // open: cin, cout
  Adder #(.width(32)) adder_2 (.a(multiplexer_1_out), .b(shifter_1_out), .out(adder_2_out));  // open: cin, cout
  Shifter #(.width(32), .shift("ar")) shifter_1 (.in(immz), .\dist (5'b00010), .out(shifter_1_out));
  Multiplexer #(.width(32), .enable("false")) multiplexer_2 (
    .in0(INSTRUCTION), .in1(32'h13), .out({func7, INSTRUCTIONz[24:15], func3, INSTRUCTIONz[11:0]}),
    .sel(or_1_out));
  or or_1 (or_1_out, bSelz, jSelz);
  Multiplexer #(.width(21), .enable("false")) multiplexer_3 (
    .in0({21{1'b0}}), .in1({21{1'b1}}), .out(multiplexer_3_out), .sel(func7[6]));
  Multiplexer #(.width(21), .enable("false")) multiplexer_4 (
    .in0({21{1'b0}}), .in1({21{1'b1}}), .out(multiplexer_4_out), .sel(func7[6]));
  Multiplexer #(.width(20), .enable("false")) multiplexer_5 (
    .in0({20{1'b0}}), .in1({20{1'b1}}), .out(multiplexer_5_out), .sel(func7[6]));
  Multiplexer #(.width(12), .enable("false")) multiplexer_6 (
    .in0({12{1'b0}}), .in1({12{1'b1}}), .out(multiplexer_6_out), .sel(func7[6]));
  Multiplexer #(.width(32), .enable("false")) multiplexer_7 (
    .in0(adder_1_out), .in1(adder_2_out), .out(multiplexer_7_out), .sel(bSelz));
  Register #(.width(5)) register_4 (.D(INSTRUCTIONz[11:7]), .clk(CLOCK), .Q(rdz));  // open: en, clr
  Register #(.width(32)) register_5 (.D(imm), .clk(CLOCK), .Q(immz));  // open: en, clr
  Register #(.width(32)) register_6 (.D(J), .clk(CLOCK), .Q(Jz));  // open: en, clr
  Register #(.width(1)) register_7 (.D(jSel), .clk(CLOCK), .Q(jSelz));  // open: en, clr
  Register #(.width(1)) register_8 (.D(bSel), .clk(CLOCK), .Q(bSelz));  // open: en, clr
  Multiplexer #(.width(32), .enable("false")) multiplexer_8 (.in0(multiplexer_7_out), .in1(Jz), .out(PC), .sel(jSelz));
  Multiplexer #(.select(3), .width(32), .enable("false")) multiplexer_9 (
    .in0({multiplexer_3_out, func7[5:0], INSTRUCTIONz[24:20]}),
    .in1({multiplexer_4_out, func7[5:0], INSTRUCTIONz[11:7]}),
    .in3({multiplexer_5_out, INSTRUCTIONz[7], func7[5:0], INSTRUCTIONz[11:8], 1'b0}),
    .in4({func7, INSTRUCTIONz[24:15], func3, {12{1'b0}}}),
    .in5({func7, INSTRUCTIONz[24:15], func3, {12{1'b0}}}),
    .in7({multiplexer_6_out, INSTRUCTIONz[19:15], func3, INSTRUCTIONz[20], func7[5:0], INSTRUCTIONz[24:21], 1'b0}),
    .out(imm), .sel({INSTRUCTIONz[2], INSTRUCTIONz[6:5]}));  // open: in2, in6
  Comparator #(.width(5)) comparator_1 (.a(INSTRUCTIONz[24:20]), .b(rdz), .eq(comparator_1_eq));  // open: gt, lt
  Multiplexer #(.width(32), .enable("false")) multiplexer_10 (
    .in0(RS2), .in1(WriteData), .out(multiplexer_10_out), .sel(comparator_1_eq));
  Comparator #(.width(5)) comparator_2 (.a(INSTRUCTIONz[19:15]), .b(rdz), .eq(comparator_2_eq));  // open: gt, lt
  Multiplexer #(.width(32), .enable("false")) multiplexer_11 (
    .in0(RS1), .in1(WriteData), .out(multiplexer_11_out), .sel(comparator_2_eq));
  Multiplexer #(.width(32), .enable("false")) multiplexer_12 (
    .in0(RS2), .in1(WriteData), .out(multiplexer_12_out), .sel(comparator_3_eq));
  Comparator #(.width(5)) comparator_3 (.a(INSTRUCTIONz[24:20]), .b(rdz), .eq(comparator_3_eq));  // open: gt, lt
  Comparator #(.width(7)) comparator_4 (.a(7'b0100011), .b(INSTRUCTIONz[6:0]), .eq(comparator_4_eq));  // open: gt, lt
  Comparator #(.width(7)) comparator_5 (.a(INSTRUCTIONz[6:0]), .b(7'b0110011), .eq(comparator_5_eq));  // open: gt, lt
  Comparator #(.width(7)) comparator_6 (.a(INSTRUCTIONz[6:0]), .b(7'b0000011), .eq(comparator_6_eq));  // open: gt, lt
  Comparator #(.width(7)) comparator_7 (.a(INSTRUCTIONz[6:0]), .b(7'b0010011), .eq(comparator_7_eq));  // open: gt, lt
  Comparator #(.width(7)) comparator_8 (.a(INSTRUCTIONz[6:0]), .b(7'b0010111), .eq(comparator_8_eq));  // open: gt, lt
  Comparator #(.width(7)) comparator_9 (.a(INSTRUCTIONz[6:0]), .b(7'b0110111), .eq(comparator_9_eq));  // open: gt, lt
  Comparator #(.width(7)) comparator_10 (.a(INSTRUCTIONz[6:0]), .b(7'b1101111), .eq(comparator_10_eq));  // open: gt, lt
  Comparator #(.width(7)) comparator_11 (.a(INSTRUCTIONz[6:0]), .b(7'b1100111), .eq(comparator_11_eq));  // open: gt, lt
  Comparator #(.width(5)) comparator_12 (.a(INSTRUCTIONz[19:15]), .b(rdz), .eq(comparator_12_eq));  // open: gt, lt
  Shifter #(.width(32), .shift("ar")) shifter_2 (.in(imm), .\dist (5'b00010), .out(shifter_2_out));
  Comparator #(.width(32)) comparator_13 (
    .a(multiplexer_11_out), .b(multiplexer_12_out), .eq(beq_sign), .lt(blt_sign));  // open: gt
  Comparator #(.width(32), .mode("unsigned")) comparator_14 (
    .a(multiplexer_11_out), .b(multiplexer_12_out), .lt(bltu_sign));  // open: gt, eq
  or or_2 (RegWEn, comparator_5_eq, comparator_6_eq, comparator_7_eq, comparator_8_eq, comparator_9_eq, comparator_10_eq, comparator_11_eq);
  Multiplexer #(.width(32), .enable("false")) multiplexer_13 (
    .in0(RS1), .in1(WriteData), .out(multiplexer_13_out), .sel(comparator_12_eq));
  Shifter #(.width(32), .shift("ar")) shifter_3 (.in(multiplexer_13_out), .\dist (5'b00010), .out(jalr));
  Adder #(.width(32)) adder_3 (.a(FETCH_ADDRESS), .b(shifter_2_out), .out(uj));  // open: cin, cout
  not not_1 (bne_sign, beq_sign);
  not not_2 (bgeu_sign, bltu_sign);
  mem_main DMEM (
    .WriteAddr(aluz), .WriteData(multiplexer_10_out), .MemRW(comparator_4_eq), .ReadData(ReadData),
    .clk(CLOCK));
  regfile_main RegFile (
    .rs2(INSTRUCTIONz[24:20]), .rd(rdz), .Read_Data_1(RS1), .Read_Data_2(RS2), .ra(ra), .sp(sp), .t0(t0),
    .t1(t1), .t2(t2), .s0(s0), .s1(s1), .a0(a0), .rs1(INSTRUCTIONz[19:15]), .Write_Data(WriteData),
    .RegWEn(RegWEnz), .clk(CLOCK));
  Comparator #(.width(7)) comparator_15 (.a(INSTRUCTIONz[6:0]), .b(7'b0000011), .eq(comparator_15_eq));  // open: gt, lt
  Comparator #(.width(7)) comparator_16 (.a(INSTRUCTIONz[6:0]), .b(7'b1101111), .eq(comparator_16_eq));  // open: gt, lt
  Comparator #(.width(7)) comparator_17 (.a(INSTRUCTIONz[6:0]), .b(7'b1100111), .eq(comparator_17_eq));  // open: gt, lt
  Comparator #(.width(7)) comparator_18 (.a(INSTRUCTIONz[6:0]), .b(7'b1100111), .eq(comparator_18_eq));  // open: gt, lt
  Comparator #(.width(7)) comparator_19 (.a(INSTRUCTIONz[6:0]), .b(7'b1101111), .eq(comparator_19_eq));  // open: gt, lt
  Comparator #(.width(3)) comparator_20 (.a(func3), .b(3'b000), .eq(comparator_20_eq));  // open: gt, lt
  Comparator #(.width(3)) comparator_21 (.a(func3), .b(3'b100), .eq(comparator_21_eq));  // open: gt, lt
  Comparator #(.width(3)) comparator_22 (.a(func3), .b(3'b111), .eq(comparator_22_eq));  // open: gt, lt
  Comparator #(.width(3)) comparator_23 (.a(func3), .b(3'b110), .eq(comparator_23_eq));  // open: gt, lt
  Comparator #(.width(3)) comparator_24 (.a(func3), .b(3'b001), .eq(comparator_24_eq));  // open: gt, lt
  assign bit_extender_1_out = {{1{comparator_15_eq}}, comparator_15_eq};  // Bit_Extender bit_extender_1
  assign bit_extender_2_out = {{1{comparator_16_eq}}, comparator_16_eq};  // Bit_Extender bit_extender_2
  assign bit_extender_3_out = {{1{comparator_17_eq}}, comparator_17_eq};  // Bit_Extender bit_extender_3
  or or_3 (jSel, comparator_18_eq, comparator_19_eq);
  assign bit_extender_4_out = {{31{comparator_18_eq}}, comparator_18_eq};  // Bit_Extender bit_extender_4
  assign and_1_out = bit_extender_4_out & jalr;  // AND_Gate and_1, 32 bits wide
  assign bit_extender_5_out = {{31{comparator_19_eq}}, comparator_19_eq};  // Bit_Extender bit_extender_5
  assign and_2_out = bit_extender_5_out & uj;  // AND_Gate and_2, 32 bits wide
  and and_3 (and_3_out, comparator_20_eq, beq_sign);
  and and_4 (and_4_out, comparator_21_eq, blt_sign);
  and and_5 (and_5_out, comparator_22_eq, bgeu_sign);
  and and_6 (and_6_out, comparator_23_eq, bltu_sign);
  and and_7 (and_7_out, comparator_24_eq, bne_sign);
  assign and_8_out = bit_extender_1_out & 2'b01;  // AND_Gate and_8, 2 bits wide
  assign and_9_out = bit_extender_2_out & 2'b10;  // AND_Gate and_9, 2 bits wide
  assign and_10_out = bit_extender_3_out & 2'b10;  // AND_Gate and_10, 2 bits wide
  assign J = and_1_out | and_2_out;  // OR_Gate or_4, 32 bits wide
  or or_5 (or_5_out, and_3_out, and_4_out, and_5_out, and_6_out, and_7_out);
  Comparator #(.width(5)) comparator_25 (.a(INSTRUCTIONz[19:15]), .b(rdz), .eq(comparator_25_eq));  // open: gt, lt
  Comparator #(.width(5)) comparator_26 (.a(rdz), .b({5{1'b0}}), .eq(comparator_26_eq));  // open: gt, lt
  assign StoreSel = and_8_out | and_9_out | and_10_out;  // OR_Gate or_6, 2 bits wide
  Comparator #(.width(7)) comparator_27 (.a(INSTRUCTIONz[6:0]), .b(7'b1100011), .eq(comparator_27_eq));  // open: gt, lt
  and and_11 (and_11_out, comparator_25_eq, not_3_out);
  not not_3 (not_3_out, comparator_26_eq);
  Multiplexer #(.width(32), .enable("false")) multiplexer_14 (
    .in0(RS2), .in1(WriteData), .out(multiplexer_14_out), .sel(comparator_28_eq));
  Comparator #(.width(5)) comparator_28 (.a(INSTRUCTIONz[24:20]), .b(rdz), .eq(comparator_28_eq));  // open: gt, lt
  Adder #(.width(32)) adder_4 (.a(32'h4), .b(shifter_4_out), .out(adder_4_out));  // open: cin, cout
  Shifter #(.width(32)) shifter_4 (.in(FETCH_ADDRESS), .\dist (5'b00010), .out(shifter_4_out));
  and and_12 (bSel, comparator_27_eq, or_5_out);
  Multiplexer #(.width(32), .enable("false")) multiplexer_15 (
    .in0(RS1), .in1(WriteData), .out(multiplexer_15_out), .sel(and_11_out));
  Comparator #(.width(7)) comparator_29 (.a(7'b0110011), .b(INSTRUCTIONz[6:0]), .eq(comparator_29_eq));  // open: gt, lt
  Register #(.width(32)) register_9 (.D(multiplexer_16_out), .clk(CLOCK), .Q(WriteData));  // open: en, clr
  Multiplexer #(.select(2), .width(32), .enable("false")) multiplexer_16 (
    .in0(aluz), .in1(load), .in2(adder_4_out), .out(multiplexer_16_out), .sel(StoreSel));  // open: in3
  Multiplexer #(.width(32), .enable("false")) multiplexer_17 (
    .in0(multiplexer_15_out), .in1(shifter_5_out), .out(multiplexer_17_out), .sel(auipc));
  Shifter #(.width(32)) shifter_5 (.in(FETCH_ADDRESS), .\dist (5'b00010), .out(shifter_5_out));
  Multiplexer #(.width(32), .enable("false")) multiplexer_18 (
    .in0(imm), .in1(multiplexer_14_out), .out(multiplexer_18_out), .sel(comparator_29_eq));
  alu alu_1 (.A(multiplexer_17_out), .B(multiplexer_18_out), .ALUSel(ALUSel), .Result(aluz));
  Comparator #(.width(5)) comparator_30 (
    .a({func3, func7[5], func7[0]}), .b({5{1'b0}}), .eq(comparator_30_eq));  // open: gt, lt
  Comparator #(.width(5)) comparator_31 (
    .a({func3, func7[5], func7[0]}), .b(5'b00001), .eq(comparator_31_eq));  // open: gt, lt
  Comparator #(.width(5)) comparator_32 (
    .a({func3, func7[5], func7[0]}), .b(5'b00010), .eq(comparator_32_eq));  // open: gt, lt
  Comparator #(.width(5)) comparator_33 (
    .a({func3, func7[5], func7[0]}), .b(5'b00100), .eq(comparator_33_eq));  // open: gt, lt
  Comparator #(.width(5)) comparator_34 (
    .a({func3, func7[5], func7[0]}), .b(5'b00101), .eq(comparator_34_eq));  // open: gt, lt
  Comparator #(.width(5)) comparator_35 (
    .a({func3, func7[5], func7[0]}), .b(5'b01101), .eq(comparator_35_eq));  // open: gt, lt
  Comparator #(.width(5)) comparator_36 (
    .a({func3, func7[5], func7[0]}), .b(5'b10000), .eq(comparator_36_eq));  // open: gt, lt
  Comparator #(.width(5)) comparator_37 (
    .a({func3, func7[5], func7[0]}), .b(5'b10001), .eq(comparator_37_eq));  // open: gt, lt
  Comparator #(.width(5)) comparator_38 (
    .a({func3, func7[5], func7[0]}), .b(5'b10101), .eq(comparator_38_eq));  // open: gt, lt
  Comparator #(.width(5)) comparator_39 (
    .a({func3, func7[5], func7[0]}), .b(5'b10100), .eq(comparator_39_eq));  // open: gt, lt
  Comparator #(.width(5)) comparator_40 (
    .a({func3, func7[5], func7[0]}), .b(5'b11000), .eq(comparator_40_eq));  // open: gt, lt
  Comparator #(.width(5)) comparator_41 (
    .a({func3, func7[5], func7[0]}), .b(5'b11101), .eq(comparator_41_eq));  // open: gt, lt
  Comparator #(.width(5)) comparator_42 (
    .a({func3, func7[5], func7[0]}), .b(5'b11100), .eq(comparator_42_eq));  // open: gt, lt
  assign bit_extender_6_out = {{3{comparator_30_eq}}, comparator_30_eq};  // Bit_Extender bit_extender_6
  assign bit_extender_7_out = {{3{comparator_31_eq}}, comparator_31_eq};  // Bit_Extender bit_extender_7
  assign bit_extender_8_out = {{3{comparator_32_eq}}, comparator_32_eq};  // Bit_Extender bit_extender_8
  assign bit_extender_9_out = {{3{comparator_33_eq}}, comparator_33_eq};  // Bit_Extender bit_extender_9
  assign bit_extender_10_out = {{3{comparator_34_eq}}, comparator_34_eq};  // Bit_Extender bit_extender_10
  assign bit_extender_11_out = {{3{comparator_35_eq}}, comparator_35_eq};  // Bit_Extender bit_extender_11
  assign bit_extender_12_out = {{3{comparator_36_eq}}, comparator_36_eq};  // Bit_Extender bit_extender_12
  assign bit_extender_13_out = {{3{comparator_37_eq}}, comparator_37_eq};  // Bit_Extender bit_extender_13
  assign bit_extender_14_out = {{3{comparator_38_eq}}, comparator_38_eq};  // Bit_Extender bit_extender_14
  assign bit_extender_15_out = {{3{comparator_39_eq}}, comparator_39_eq};  // Bit_Extender bit_extender_15
  assign bit_extender_16_out = {{3{comparator_40_eq}}, comparator_40_eq};  // Bit_Extender bit_extender_16
  assign bit_extender_17_out = {{3{comparator_41_eq}}, comparator_41_eq};  // Bit_Extender bit_extender_17
  assign bit_extender_18_out = {{3{comparator_42_eq}}, comparator_42_eq};  // Bit_Extender bit_extender_18
  assign and_13_out = bit_extender_6_out & 4'b0000;  // AND_Gate and_13, 4 bits wide
  assign and_14_out = bit_extender_7_out & 4'b0001;  // AND_Gate and_14, 4 bits wide
  assign and_15_out = bit_extender_8_out & 4'b0010;  // AND_Gate and_15, 4 bits wide
  assign and_16_out = bit_extender_9_out & 4'b0011;  // AND_Gate and_16, 4 bits wide
  assign and_17_out = bit_extender_10_out & 4'b0100;  // AND_Gate and_17, 4 bits wide
  assign and_18_out = bit_extender_11_out & 4'b0101;  // AND_Gate and_18, 4 bits wide
  assign and_19_out = bit_extender_12_out & 4'b0110;  // AND_Gate and_19, 4 bits wide
  assign and_20_out = bit_extender_13_out & 4'b0111;  // AND_Gate and_20, 4 bits wide
  assign and_21_out = bit_extender_14_out & 4'b1000;  // AND_Gate and_21, 4 bits wide
  assign and_22_out = bit_extender_15_out & 4'b1001;  // AND_Gate and_22, 4 bits wide
  assign and_23_out = bit_extender_16_out & 4'b1010;  // AND_Gate and_23, 4 bits wide
  assign and_24_out = bit_extender_17_out & 4'b1011;  // AND_Gate and_24, 4 bits wide
  assign and_25_out = bit_extender_18_out & 4'b1100;  // AND_Gate and_25, 4 bits wide
  assign Selr = and_13_out | and_14_out | and_15_out | and_16_out | and_17_out | and_18_out | and_19_out | and_20_out | and_21_out | and_22_out | and_23_out | and_24_out | and_25_out;  // OR_Gate or_7, 4 bits wide
  Shifter #(.width(32)) shifter_6 (.in(ReadData), .\dist (5'b11000), .out(shifter_6_out));
  Shifter #(.width(32)) shifter_7 (.in(ReadData), .\dist (5'b10000), .out(shifter_7_out));
  Shifter #(.width(32), .shift("ar")) shifter_8 (.in(shifter_6_out), .\dist (5'b11000), .out(shifter_8_out));
  Shifter #(.width(32), .shift("lr")) shifter_9 (.in(shifter_6_out), .\dist (5'b11000), .out(shifter_9_out));
  Shifter #(.width(32), .shift("ar")) shifter_10 (.in(shifter_7_out), .\dist (5'b10000), .out(shifter_10_out));
  Shifter #(.width(32), .shift("lr")) shifter_11 (.in(shifter_7_out), .\dist (5'b10000), .out(shifter_11_out));
  Comparator #(.width(7)) comparator_43 (.a(INSTRUCTIONz[6:0]), .b(7'b0110011), .eq(comparator_43_eq));  // open: gt, lt
  Comparator #(.width(7)) comparator_44 (.a(INSTRUCTIONz[6:0]), .b(7'b0010011), .eq(comparator_44_eq));  // open: gt, lt
  Comparator #(.width(7)) comparator_45 (.a(INSTRUCTIONz[6:0]), .b(7'b0110111), .eq(comparator_45_eq));  // open: gt, lt
  Comparator #(.width(7)) comparator_46 (.a(INSTRUCTIONz[6:0]), .b(7'b0010111), .eq(auipc));  // open: gt, lt
  Comparator #(.width(7)) comparator_47 (.a(INSTRUCTIONz[6:0]), .b(7'b0000011), .eq(comparator_47_eq));  // open: gt, lt
  Multiplexer #(.select(3), .width(32), .enable("false")) multiplexer_19 (
    .in0(shifter_8_out), .in1(shifter_10_out), .in2(ReadData), .in4(shifter_9_out), .in5(shifter_11_out),
    .out(load), .sel(func3));  // open: in3, in6, in7
  assign bit_extender_19_out = {{3{comparator_43_eq}}, comparator_43_eq};  // Bit_Extender bit_extender_19
  assign bit_extender_20_out = {{3{comparator_44_eq}}, comparator_44_eq};  // Bit_Extender bit_extender_20
  assign bit_extender_21_out = {{3{comparator_45_eq}}, comparator_45_eq};  // Bit_Extender bit_extender_21
  assign bit_extender_22_out = {{3{auipc}}, auipc};  // Bit_Extender bit_extender_22
  assign bit_extender_23_out = {{3{comparator_47_eq}}, comparator_47_eq};  // Bit_Extender bit_extender_23
  Comparator #(.width(3)) comparator_48 (.a(func3), .b(3'b000), .eq(comparator_48_eq));  // open: gt, lt
  Comparator #(.width(3)) comparator_49 (.a(func3), .b(3'b001), .eq(comparator_49_eq));  // open: gt, lt
  Comparator #(.width(3)) comparator_50 (.a(func3), .b(3'b010), .eq(comparator_50_eq));  // open: gt, lt
  Comparator #(.width(3)) comparator_51 (.a(func3), .b(3'b100), .eq(comparator_51_eq));  // open: gt, lt
  Comparator #(.width(3)) comparator_52 (.a(func3), .b(3'b101), .eq(comparator_52_eq));  // open: gt, lt
  Comparator #(.width(3)) comparator_53 (.a(func3), .b(3'b110), .eq(comparator_53_eq));  // open: gt, lt
  Comparator #(.width(3)) comparator_54 (.a(func3), .b(3'b111), .eq(comparator_54_eq));  // open: gt, lt
  assign and_26_out = bit_extender_19_out & Selr;  // AND_Gate and_26, 4 bits wide
  assign and_27_out = bit_extender_20_out & Seli;  // AND_Gate and_27, 4 bits wide
  assign and_28_out = bit_extender_21_out & 4'b1101;  // AND_Gate and_28, 4 bits wide
  assign and_29_out = bit_extender_22_out & 4'b0000;  // AND_Gate and_29, 4 bits wide
  assign and_30_out = bit_extender_23_out & 4'b0000;  // AND_Gate and_30, 4 bits wide
  assign bit_extender_24_out = {{3{comparator_48_eq}}, comparator_48_eq};  // Bit_Extender bit_extender_24
  assign and_31_out = bit_extender_24_out & 4'b0000;  // AND_Gate and_31, 4 bits wide
  assign bit_extender_25_out = {{3{comparator_49_eq}}, comparator_49_eq};  // Bit_Extender bit_extender_25
  assign and_32_out = bit_extender_25_out & 4'b0011;  // AND_Gate and_32, 4 bits wide
  assign bit_extender_26_out = {{3{comparator_50_eq}}, comparator_50_eq};  // Bit_Extender bit_extender_26
  assign and_33_out = bit_extender_26_out & 4'b1110;  // AND_Gate and_33, 4 bits wide
  assign bit_extender_27_out = {{3{comparator_51_eq}}, comparator_51_eq};  // Bit_Extender bit_extender_27
  assign and_34_out = bit_extender_27_out & 4'b0110;  // AND_Gate and_34, 4 bits wide
  assign bit_extender_28_out = {{3{comparator_52_eq}}, comparator_52_eq};  // Bit_Extender bit_extender_28
  assign and_35_out = bit_extender_28_out & 4'b1001;  // AND_Gate and_35, 4 bits wide
  assign bit_extender_29_out = {{3{comparator_53_eq}}, comparator_53_eq};  // Bit_Extender bit_extender_29
  assign and_36_out = bit_extender_29_out & 4'b1010;  // AND_Gate and_36, 4 bits wide
  assign bit_extender_30_out = {{3{comparator_54_eq}}, comparator_54_eq};  // Bit_Extender bit_extender_30
  assign and_37_out = bit_extender_30_out & 4'b1100;  // AND_Gate and_37, 4 bits wide
  assign ALUSel = and_26_out | and_27_out | and_28_out | and_29_out | and_30_out;  // OR_Gate or_8, 4 bits wide
  assign Seli = and_31_out | and_32_out | and_33_out | and_34_out | and_35_out | and_36_out | and_37_out;  // OR_Gate or_9, 4 bits wide

  // Other names for the same wires on the sheet: rs2_t[4:0] = INSTRUCTIONz[24:20]; rs1_t[4:0] = INSTRUCTIONz[19:15];
  //   rd[4:0] = INSTRUCTIONz[11:7]; INSTRUCTIONz (some bits) = {func7, func3};
  //   selr_t[4:0] = {func3, func7[5], func7[0]}; seli_t[3:0] = {func3, func7[5]}; WriteAddr[31:0] = aluz; clk = CLOCK;
  //   opcode[6:0] = INSTRUCTIONz[6:0]; fetch_addr[31:0] = FETCH_ADDRESS; pc_t[31:0] = FETCH_ADDRESS

  // Notes on the sheet:
  //   I
  //   S
  //   SB
  //   U
  //   UJ
  //   Output
  //   PC
  //   Instruction
  //   Imm Generator
  //   Update in Reg
  //   Update in Reg
  //   Inputs/Outputs from run.circ. DO NOT MOVE THESE.
  //   Inputs
  //   Mem
  //   Mem
  //   determine Type
  //   J Type
  //   J Type
  //   IO Interface
  //   IO Interface
  //   SB Type
  //   Inputs/Outputs from run.circ. DO NOT MOVE THESE.
  //   not x0
  //   check quick use
  //   check quick use
  //   lw
  //   normal
  //   J Type
  //   Execute
  //   Execute
  //   determine imm
  //   add
  //   mul
  //   sub
  //   sll
  //   mulh
  //   mulhu
  //   xor
  //   div
  //   divu
  //   srl
  //   or
  //   remu
  //   and
  //   Load
  //   Load
  //   lui
  //   auipc
  //   addi
  //   R/I Type
  //   slli
  //   slti
  //   xori
  //   srli
  //   ori
  //   andi
endmodule
